// Logisim project calculadora.circ as structural Verilog: 3 circuits, main circuit full adder
// +
module full_adder (
  input  A,
  input  B,
  input  Cin,
  output out_4,
  output out_5
);

  wire and_1_out, and_2_out, and_3_out, and_4_out, not_1_out, not_2_out, not_3_out, xor_1_out;

  not not_1 (not_1_out, A);
  not not_2 (not_2_out, B);
  not not_3 (not_3_out, Cin);
  xor xor_1 (xor_1_out, A, B);
  and and_1 (and_1_out, not_1_out, B, Cin);
  and and_2 (and_2_out, A, not_2_out, Cin);
  and and_3 (and_3_out, A, B, not_3_out);
  and and_4 (and_4_out, A, B, Cin);
  xor xor_2 (out_4, xor_1_out, Cin);
  or or_1 (out_5, and_1_out, and_2_out, and_3_out, and_4_out);
endmodule

module main (
);

  full_adder full_adder_1 ();  // open: A, B, Cin, out_4, out_5
  full_subtractor full_subtractor_1 ();  // open: A, B, Bin, out_4, out_5
endmodule

// -
module full_subtractor (
  input  A,
  input  B,
  input  Bin,
  output out_4,
  output out_5
);

  wire and_1_out, and_2_out, and_3_out, not_1_out, xor_1_out;

  xor xor_1 (xor_1_out, A, B);
  not not_1 (not_1_out, A);
  and and_1 (and_1_out, not_1_out, B);
  and and_2 (and_2_out, not_1_out, Bin);
  and and_3 (and_3_out, B, Bin);
  xor xor_2 (out_4, xor_1_out, Bin);
  or or_1 (out_5, and_1_out, and_2_out, and_3_out);
endmodule
